# Fritzing sketch Circuit shema (saved by Fritzing 0.9.5d)

parts:
  Part1 = Motor Driver 1A Dual TB6612FNG
  U2 = LM2596 step down module
  VCC1 = Battery
  Part2 = InvenSense MPU6050
  M1 = DC Motor
  M2 = DC Motor
  S1 = Toggle Switch [package=THT]
  M3 = DOIT Esp32 DevKit v1 (30 pins long, 11 pins width) [part_number=ESP32S-PIN30]

nets:
  N1: Part1.B01, M2.pin_1
  N2: Part1.B02, M2.pin_2
  N3: Part1.A02, M1.pin_2
  N4: Part1.A01, M1.pin_1
  VCC: Part1.VCC, U2.OUT+, M3.VIN
  N5: Part1.VM, U2.IN+, S1.COM, S1.L2
  N6: Part1.PWMA, M3.D33
  N7: Part1.AIN2, M3.D25
  N8: Part1.AIN1, M3.D26
  N9: Part1.STBY, M3.D27
  N10: Part1.BIN1, M3.D14
  N11: Part1.BIN2, M3.D12
  N12: Part1.PWMB, M3.D13
  GND: Part1.GND, U2.IN-, U2.OUT-, VCC1.-, Part2.GND, M3.GND
  N13: VCC1.+, S1.L1
  VCC_2: Part2.VCC, M3.3V3
  N14: Part2.SCL, M3.D22
  N15: Part2.SDA, M3.D21

custom parts:
  LM2596 step down module: LM2596 DC-DC step down power supply module 3 A.
  DOIT Esp32 DevKit v1 (30 pins long, 11 pins width): The DOIT Esp32 DevKit v1 is one of the development board created by DOIT to evaluate the ESP-WROOM-32 module. It is based on the ESP32 microcontroller that boasts Wifi, Bluetooth, Ethernet and Low Power support all in a single chip. (vanepp) made breadboard work, adjusted pin numbering and labels and reduced size of schematic and cleaned up pcb. This chip is 30pins long (2 x15) and 11 pins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
